// Digital circuit irq-logic_chip.dig as structural Verilog
module irq_logic_chip (
  input  nIRQ14,
  input  nIRQ13,
  input  nIRQ12,
  input  nIRQ11,
  input  nIRQ10,
  input  nIRQ9,
  input  nIRQ3,
  input  nIRQ2,
  input  nIRQ1,
  input  nIRQ0,
  input  nIRQ4,
  input  nIRQ5,
  input  nIRQ6,
  input  nIRQ7,
  input  nIRQ8,
  input  nRD,
  input  nIRQ_EN,
  input  nWR,
  input  D0,
  input  D1,
  input  D2,
  input  D3,
  input  Q
);

  wire _7485_1_pin7, _74148_1_pin5, _74148_1_pin6, _74148_1_pin7, _74148_1_pin9, _74148_2_pin6,
       _74148_2_pin7, _74148_2_pin9, _74148_2_pin14, _74574_1_pin16, _74574_1_pin17, _74574_1_pin18,
       _74574_1_pin19, _74574_2_pin12, _74574_2_pin13, _74574_2_pin14, _74574_2_pin15, _74574_2_pin16,
       _74574_2_pin17, _74574_2_pin18, _74574_2_pin19, nand_1_out, nand_2_out, nand_3_out, nand_4_out,
       nor_1_out, nor_2_out, nor_3_out, nor_4_out;

  nor nor_1 (nor_1_out, nRD, nIRQ_EN);
  nor nor_2 (nor_2_out, nIRQ_EN, nWR);
  _74148 _74148_1 (
    .pin1(nIRQ11), .pin2(nIRQ10), .pin3(nIRQ9), .pin4(nIRQ8), .pin5(_74148_1_pin5), .pin6(_74148_1_pin6),
    .pin7(_74148_1_pin7), .pin8(1'b0), .pin9(_74148_1_pin9), .pin10(1'b1), .pin11(nIRQ14), .pin12(nIRQ13),
    .pin13(nIRQ12), .pin16(1'b1));  // open: pin14, pin15
  _74148 _74148_2 (
    .pin1(nIRQ3), .pin2(nIRQ2), .pin3(nIRQ1), .pin4(nIRQ0), .pin5(1'b0), .pin6(_74148_2_pin6),
    .pin7(_74148_2_pin7), .pin8(1'b0), .pin9(_74148_2_pin9), .pin10(nIRQ7), .pin11(nIRQ6), .pin12(nIRQ5),
    .pin13(nIRQ4), .pin14(_74148_2_pin14), .pin15(_74148_1_pin5), .pin16(1'b1));
  _74574 _74574_1 (
    .pin1(1'b0), .pin2(D0), .pin3(D1), .pin4(D2), .pin5(D3), .pin6(1'b0), .pin7(1'b0), .pin8(1'b0),
    .pin9(1'b0), .pin10(1'b0), .pin11(nor_2_out), .pin16(_74574_1_pin16), .pin17(_74574_1_pin17),
    .pin18(_74574_1_pin18), .pin19(_74574_1_pin19), .pin20(1'b1));  // open: pin12, pin13, pin14, pin15
  nand nand_1 (nand_1_out, _74148_1_pin6, _74148_2_pin6);
  nand nand_2 (nand_2_out, _74148_1_pin7, _74148_2_pin7);
  nand nand_3 (nand_3_out, _74148_1_pin9, _74148_2_pin9);
  nand nand_4 (nand_4_out, _74148_2_pin14, _74148_2_pin14);
  nor nor_3 (nor_3_out, nor_1_out, nor_1_out);
  _74574 _74574_2 (
    .pin1(nor_3_out), .pin2(nand_1_out), .pin3(nand_2_out), .pin4(nand_1_out), .pin5(nand_4_out),
    .pin6(_74574_1_pin19), .pin7(_74574_1_pin18), .pin8(_74574_1_pin17), .pin9(_74574_1_pin16), .pin10(1'b0),
    .pin11(Q), .pin12(_74574_2_pin12), .pin13(_74574_2_pin13), .pin14(_74574_2_pin14),
    .pin15(_74574_2_pin15), .pin16(_74574_2_pin16), .pin17(_74574_2_pin17), .pin18(_74574_2_pin18),
    .pin19(_74574_2_pin19), .pin20(1'b1));
  _7485 _7485_1 (
    .pin1(nand_4_out), .pin2(1'b0), .pin3(1'b0), .pin4(1'b0), .pin7(_7485_1_pin7), .pin8(1'b0),
    .pin9(nand_3_out), .pin10(_74574_1_pin19), .pin11(nand_2_out), .pin12(_74574_1_pin18),
    .pin13(_74574_1_pin17), .pin14(nand_1_out), .pin15(_74574_1_pin16), .pin16(1'b1));  // open: pin5, pin6
  LED led_1 (.in(_74574_2_pin19));
  LED led_2 (.in(_74574_2_pin18));
  LED led_3 (.in(_74574_2_pin17));
  LED led_4 (.in(_74574_2_pin16));
  LED led_5 (.in(_74574_2_pin15));
  LED led_6 (.in(_74574_2_pin14));
  LED led_7 (.in(_74574_2_pin13));
  LED led_8 (.in(_74574_2_pin12));
  nor nor_4 (nor_4_out, _7485_1_pin7, _7485_1_pin7);
  LED nIRQ (.in(nor_4_out));

  // Notes on the sheet:
  //   nIRQ14: default 1
  //   nIRQ13: default 1
  //   nIRQ12: default 1
  //   nIRQ11: default 1
  //   nIRQ10: default 1
  //   nIRQ9: default 1
  //   nIRQ3: default 1
  //   nIRQ2: default 1
  //   nIRQ1: default 1
  //   nIRQ0: default 1
  //   nIRQ4: default 1
  //   nIRQ5: default 1
  //   nIRQ6: default 1
  //   nIRQ7: default 1
  //   nIRQ8: default 1
  //   nRD: default 1
  //   nIRQ_EN: default 1
  //   nWR: default 1
  //   Q: default 1
endmodule
