// Digital circuit irq-logic.dig as structural Verilog
module irq_logic (
  input  D0,
  input  D1,
  input  D2,
  input  D3,
  input  D4,
  input  D5,
  input  D6,
  input  D7,
  input  R0,
  input  R1,
  input  W0,
  input  W1,
  input  MAP_RD,
  input  MEM_WR,
  input  MEM_RD
);

  wire _74670_1_pin6, _74670_1_pin7, _74670_1_pin9, _74670_1_pin10, _74670_2_pin6, _74670_2_pin7,
       _74670_2_pin9, _74670_2_pin10;

  _74670 _74670_1 (
    .pin1(D1), .pin2(D2), .pin3(D3), .pin4(R1), .pin5(R0), .pin6(_74670_1_pin6), .pin7(_74670_1_pin7),
    .pin8(1'b0), .pin9(_74670_1_pin9), .pin10(_74670_1_pin10), .pin11(MAP_RD), .pin12(MEM_WR), .pin13(W1),
    .pin14(W0), .pin15(D0), .pin16(1'b1));
  _74670 _74670_2 (
    .pin1(D5), .pin2(D6), .pin3(D7), .pin4(R1), .pin5(R0), .pin6(_74670_2_pin6), .pin7(_74670_2_pin7),
    .pin8(1'b0), .pin9(_74670_2_pin9), .pin10(_74670_2_pin10), .pin11(MAP_RD), .pin12(MEM_WR), .pin13(W1),
    .pin14(W0), .pin15(D4), .pin16(1'b1));
  PowerSupply powersupply_1 (.VDD(1'b1), .GND(1'b0));
  _74245 _74245_1 (
    .pin1(1'b1), .pin2(_74670_1_pin10), .pin3(_74670_1_pin9), .pin4(_74670_1_pin7), .pin5(_74670_1_pin6),
    .pin6(_74670_2_pin10), .pin7(_74670_2_pin9), .pin8(_74670_2_pin7), .pin9(_74670_2_pin6), .pin10(1'b0),
    .pin11(D7), .pin12(D6), .pin13(D5), .pin14(D4), .pin15(D3), .pin16(D2), .pin17(D1), .pin18(D0),
    .pin19(MEM_RD), .pin20(1'b1));
endmodule
